// Logisim project 839841-BR32test.circ as structural Verilog: 3 circuits, main circuit main
module BR4 (
  input  regWr,
  input  clk,
  input  reset,
  input  [31:0] busW,
  input  [1:0] RA,
  input  [1:0] RW,
  input  [1:0] RB,
  output [31:0] busA,
  output [31:0] busB
);

  wire decoder_1_out0, decoder_1_out1, decoder_1_out2, decoder_1_out3;
  wire [31:0] register_1_q, register_2_q, register_3_q, register_4_q;

  Decoder #(.select(2), .disabled(0)) decoder_1 (
    .out0(decoder_1_out0), .out1(decoder_1_out1), .out2(decoder_1_out2), .out3(decoder_1_out3), .sel(RW),
    .en(regWr));
  Register #(.width(32)) register_1 (.D(busW), .en(decoder_1_out0), .Q(register_1_q), .clk(clk), .clr(reset));
  Register #(.width(32)) register_2 (.D(busW), .en(decoder_1_out1), .Q(register_2_q), .clk(clk), .clr(reset));
  Register #(.width(32)) register_3 (.D(busW), .en(decoder_1_out2), .Q(register_3_q), .clk(clk), .clr(reset));
  Register #(.width(32)) register_4 (.D(busW), .en(decoder_1_out3), .Q(register_4_q), .clk(clk), .clr(reset));
  Multiplexer #(.select(2), .width(32), .enable("false")) multiplexer_1 (
    .in0(register_1_q), .in1(register_2_q), .in2(register_3_q), .in3(register_4_q), .out(busB), .sel(RB));
  Multiplexer #(.select(2), .width(32), .enable("false")) multiplexer_2 (
    .in0(register_1_q), .in1(register_2_q), .in2(register_3_q), .in3(register_4_q), .out(busA), .sel(RA));
endmodule

module BR32 (
  input  reset,
  input  clk,
  input  [31:0] busW,
  input  regWr,
  input  [4:0] RW,
  input  [4:0] RA,
  input  [4:0] RB,
  output [31:0] busA,
  output [31:0] busB
);

  wire decoder_1_out0, decoder_1_out1, decoder_1_out2, decoder_1_out3, decoder_1_out4, decoder_1_out5,
       decoder_1_out6, decoder_1_out7;
  wire [31:0] br4_1_busa, br4_1_busb, br4_2_busa, br4_2_busb, br4_3_busa, br4_3_busb, br4_4_busa, br4_4_busb,
       br4_5_busa, br4_5_busb, br4_6_busa, br4_6_busb, br4_7_busa, br4_7_busb, br4_8_busa, br4_8_busb;

  Decoder #(.select(3), .disabled(0)) decoder_1 (
    .out0(decoder_1_out0), .out1(decoder_1_out1), .out2(decoder_1_out2), .out3(decoder_1_out3),
    .out4(decoder_1_out4), .out5(decoder_1_out5), .out6(decoder_1_out6), .out7(decoder_1_out7),
    .sel(RW[2:0]), .en(regWr));
  BR4 br4_1 (
    .regWr(decoder_1_out0), .clk(clk), .reset(reset), .busW(busW), .RW(RW[4:3]), .RB(RB[4:3]), .RA(RA[4:3]),
    .busA(br4_1_busa), .busB(br4_1_busb));
  BR4 br4_2 (
    .regWr(decoder_1_out1), .clk(clk), .reset(reset), .busW(busW), .RW(RW[4:3]), .RB(RB[4:3]), .RA(RA[4:3]),
    .busA(br4_2_busa), .busB(br4_2_busb));
  BR4 br4_3 (
    .regWr(decoder_1_out2), .clk(clk), .reset(reset), .busW(busW), .RW(RW[4:3]), .RB(RB[4:3]), .RA(RA[4:3]),
    .busA(br4_3_busa), .busB(br4_3_busb));
  BR4 br4_4 (
    .regWr(decoder_1_out3), .clk(clk), .reset(reset), .busW(busW), .RW(RW[4:3]), .RB(RB[4:3]), .RA(RA[4:3]),
    .busA(br4_4_busa), .busB(br4_4_busb));
  BR4 br4_5 (
    .regWr(decoder_1_out4), .clk(clk), .reset(reset), .busW(busW), .RW(RW[4:3]), .RB(RB[4:3]), .RA(RA[4:3]),
    .busA(br4_5_busa), .busB(br4_5_busb));
  BR4 br4_6 (
    .regWr(decoder_1_out5), .clk(clk), .reset(reset), .busW(busW), .RW(RW[4:3]), .RB(RB[4:3]), .RA(RA[4:3]),
    .busA(br4_6_busa), .busB(br4_6_busb));
  BR4 br4_7 (
    .regWr(decoder_1_out6), .clk(clk), .reset(reset), .busW(busW), .RW(RW[4:3]), .RB(RB[4:3]), .RA(RA[4:3]),
    .busA(br4_7_busa), .busB(br4_7_busb));
  BR4 br4_8 (
    .regWr(decoder_1_out7), .clk(clk), .reset(reset), .busW(busW), .RW(RW[4:3]), .RB(RB[4:3]), .RA(RA[4:3]),
    .busA(br4_8_busa), .busB(br4_8_busb));
  Multiplexer #(.select(3), .width(32), .enable("false")) multiplexer_1 (
    .in0(br4_1_busa), .in1(br4_2_busa), .in2(br4_3_busa), .in3(br4_4_busa), .in4(br4_5_busa),
    .in5(br4_6_busa), .in6(br4_7_busa), .in7(br4_8_busa), .out(busA), .sel(RA[2:0]));
  Multiplexer #(.select(3), .width(32), .enable("false")) multiplexer_2 (
    .in0(br4_1_busb), .in1(br4_2_busb), .in2(br4_3_busb), .in3(br4_4_busb), .in4(br4_5_busb),
    .in5(br4_6_busb), .in6(br4_7_busb), .in7(br4_8_busb), .out(busB), .sel(RB[2:0]));

  // Other names for the same wires on the sheet: RA_prime[2:0] = RA[2:0]; RA_t[1:0] = RA[4:3];
  //   RB_prime[2:0] = RB[2:0]; RB_t[1:0] = RB[4:3]; RW_prime[2:0] = RW[2:0]; RW_t[1:0] = RW[4:3]
endmodule

module main (
  input  reset
);

  wire br32test_1_p5, br32test_1_p6, br32test_1_p7, br32test_1_p9, br32test_1_p11;
  wire [4:0] br32test_1_p1, br32test_1_p3, br32test_1_p10;
  wire [31:0] br32test_1_p2, br32test_1_p4, br32test_1_p12;

  // Probe on br32test_1_p7
  // Probe on br32test_1_p5
  // Probe on br32test_1_p9
  // BR32test br32test_1: pin names not known; wires that end beside it: br32test_1_p1, br32test_1_p2, br32test_1_p3, br32test_1_p4, br32test_1_p5, br32test_1_p6, br32test_1_p7, reset, br32test_1_p9, br32test_1_p10, br32test_1_p11, br32test_1_p12
  Clock clk (.out(br32test_1_p6));
  BR32 br32_1 (
    .regWr(br32test_1_p11), .reset(reset), .clk(br32test_1_p6), .busW(br32test_1_p12), .busA(br32test_1_p2),
    .busB(br32test_1_p4), .RW(br32test_1_p10), .RA(br32test_1_p1), .RB(br32test_1_p3));
endmodule
