// Logisim project 839841-multi.circ as structural Verilog: 3 circuits, main circuit main
module BR4 (
  input  regWr,
  input  clk,
  input  reset,
  input  [31:0] busW,
  input  [1:0] RA,
  input  [1:0] RW,
  input  [1:0] RB,
  output [31:0] busA,
  output [31:0] busB
);

  wire decoder_1_out0, decoder_1_out1, decoder_1_out2, decoder_1_out3;
  wire [31:0] register_1_q, register_2_q, register_3_q, register_4_q;

  Decoder #(.select(2), .disabled(0)) decoder_1 (
    .out0(decoder_1_out0), .out1(decoder_1_out1), .out2(decoder_1_out2), .out3(decoder_1_out3), .sel(RW),
    .en(regWr));
  Register #(.width(32)) register_1 (.D(busW), .en(decoder_1_out0), .Q(register_1_q), .clk(clk), .clr(reset));
  Register #(.width(32)) register_2 (.D(busW), .en(decoder_1_out1), .Q(register_2_q), .clk(clk), .clr(reset));
  Register #(.width(32)) register_3 (.D(busW), .en(decoder_1_out2), .Q(register_3_q), .clk(clk), .clr(reset));
  Register #(.width(32)) register_4 (.D(busW), .en(decoder_1_out3), .Q(register_4_q), .clk(clk), .clr(reset));
  Multiplexer #(.select(2), .width(32), .enable("false")) multiplexer_1 (
    .in0(register_1_q), .in1(register_2_q), .in2(register_3_q), .in3(register_4_q), .out(busB), .sel(RB));
  Multiplexer #(.select(2), .width(32), .enable("false")) multiplexer_2 (
    .in0(register_1_q), .in1(register_2_q), .in2(register_3_q), .in3(register_4_q), .out(busA), .sel(RA));
endmodule

module BR32 (
  input  reset,
  input  clk,
  input  [31:0] busW,
  input  regWr,
  input  [4:0] RW,
  input  [4:0] RA,
  input  [4:0] RB,
  output [31:0] busA,
  output [31:0] busB
);

  wire decoder_1_out0, decoder_1_out1, decoder_1_out2, decoder_1_out3, decoder_1_out4, decoder_1_out5,
       decoder_1_out6, decoder_1_out7;
  wire [31:0] br4_1_busa, br4_1_busb, br4_2_busa, br4_2_busb, br4_3_busa, br4_3_busb, br4_4_busa, br4_4_busb,
       br4_5_busa, br4_5_busb, br4_6_busa, br4_6_busb, br4_7_busa, br4_7_busb, br4_8_busa, br4_8_busb;

  Decoder #(.select(3), .disabled(0)) decoder_1 (
    .out0(decoder_1_out0), .out1(decoder_1_out1), .out2(decoder_1_out2), .out3(decoder_1_out3),
    .out4(decoder_1_out4), .out5(decoder_1_out5), .out6(decoder_1_out6), .out7(decoder_1_out7),
    .sel(RW[2:0]), .en(regWr));
  BR4 br4_1 (
    .regWr(decoder_1_out0), .clk(clk), .reset(reset), .busW(busW), .RW(RW[4:3]), .RB(RB[4:3]), .RA(RA[4:3]),
    .busA(br4_1_busa), .busB(br4_1_busb));
  BR4 br4_2 (
    .regWr(decoder_1_out1), .clk(clk), .reset(reset), .busW(busW), .RW(RW[4:3]), .RB(RB[4:3]), .RA(RA[4:3]),
    .busA(br4_2_busa), .busB(br4_2_busb));
  BR4 br4_3 (
    .regWr(decoder_1_out2), .clk(clk), .reset(reset), .busW(busW), .RW(RW[4:3]), .RB(RB[4:3]), .RA(RA[4:3]),
    .busA(br4_3_busa), .busB(br4_3_busb));
  BR4 br4_4 (
    .regWr(decoder_1_out3), .clk(clk), .reset(reset), .busW(busW), .RW(RW[4:3]), .RB(RB[4:3]), .RA(RA[4:3]),
    .busA(br4_4_busa), .busB(br4_4_busb));
  BR4 br4_5 (
    .regWr(decoder_1_out4), .clk(clk), .reset(reset), .busW(busW), .RW(RW[4:3]), .RB(RB[4:3]), .RA(RA[4:3]),
    .busA(br4_5_busa), .busB(br4_5_busb));
  BR4 br4_6 (
    .regWr(decoder_1_out5), .clk(clk), .reset(reset), .busW(busW), .RW(RW[4:3]), .RB(RB[4:3]), .RA(RA[4:3]),
    .busA(br4_6_busa), .busB(br4_6_busb));
  BR4 br4_7 (
    .regWr(decoder_1_out6), .clk(clk), .reset(reset), .busW(busW), .RW(RW[4:3]), .RB(RB[4:3]), .RA(RA[4:3]),
    .busA(br4_7_busa), .busB(br4_7_busb));
  BR4 br4_8 (
    .regWr(decoder_1_out7), .clk(clk), .reset(reset), .busW(busW), .RW(RW[4:3]), .RB(RB[4:3]), .RA(RA[4:3]),
    .busA(br4_8_busa), .busB(br4_8_busb));
  Multiplexer #(.select(3), .width(32), .enable("false")) multiplexer_1 (
    .in0(br4_1_busa), .in1(br4_2_busa), .in2(br4_3_busa), .in3(br4_4_busa), .in4(br4_5_busa),
    .in5(br4_6_busa), .in6(br4_7_busa), .in7(br4_8_busa), .out(busA), .sel(RA[2:0]));
  Multiplexer #(.select(3), .width(32), .enable("false")) multiplexer_2 (
    .in0(br4_1_busb), .in1(br4_2_busb), .in2(br4_3_busb), .in3(br4_4_busb), .in4(br4_5_busb),
    .in5(br4_6_busb), .in6(br4_7_busb), .in7(br4_8_busb), .out(busB), .sel(RB[2:0]));

  // Other names for the same wires on the sheet: RA_prime[2:0] = RA[2:0]; RA_t[1:0] = RA[4:3];
  //   RB_prime[2:0] = RB[2:0]; RB_t[1:0] = RB[4:3]; RW_prime[2:0] = RW[2:0]; RW_t[1:0] = RW[4:3]
endmodule

module main (
);

  wire mux_c, PC, RA, RB, RC, regWr, reloj, reset;
  wire [2:0] rom_2_data;
  wire [3:0] counter_1_q;
  wire [3:1] A_q;
  wire [4:0] RW;
  wire [30:5] rom_1_data;
  wire [31:0] A_2_q, adder_1_out, B_q, bit_extender_1_out, br32_1_busa, br32_1_busb, busW, C_q;

  Button button_1 (.out(reset));
  Clock clock_1 (.out(reloj));
  // Probe on mux_c
  // RTL1_Viewer rtl1_viewer_1: pin names not known; wires that end beside it: busW, RW, regWr
  Counter #(.width(4), .max('hf)) counter_1 (
    .count(PC), .Q(counter_1_q), .clk(reloj), .clr(reset));  // open: load, D, carry
  ROM #(.addrWidth(4), .dataWidth(32)) rom_1 (.addr(counter_1_q), .data({mux_c, rom_1_data, RW}));  // open: sel
  ROM #(.addrWidth(4), .dataWidth(3)) rom_2 (.addr({A_q, mux_c}), .data(rom_2_data));  // open: sel
  Register #(.width(3)) A (.D(rom_2_data), .Q(A_q), .clk(reloj), .clr(reset));  // open: en
  BR32 br32_1 (
    .regWr(regWr), .reset(reset), .clk(reloj), .busW(busW), .busA(br32_1_busa), .busB(br32_1_busb), .RW(RW),
    .RA(rom_1_data[14:10]), .RB(rom_1_data[9:5]));
  Register #(.width(32)) A_2 (.D(br32_1_busa), .en(RA), .Q(A_2_q), .clk(reloj), .clr(reset));
  Register #(.width(32)) B (.D(br32_1_busb), .en(RB), .Q(B_q), .clk(reloj), .clr(reset));
  Adder #(.width(32)) adder_1 (.a(A_2_q), .b(B_q), .out(adder_1_out));  // open: cin, cout
  Register #(.width(32)) C (.D(adder_1_out), .en(RC), .Q(C_q), .clk(reloj), .clr(reset));
  assign bit_extender_1_out = {{16{1'b0}}, rom_1_data[30:15]};  // Bit_Extender bit_extender_1
  ROM #(.addrWidth(4), .dataWidth(5)) rom_3 (.addr({A_q, mux_c}), .data({RA, RB, RC, regWr, PC}));  // open: sel
  Multiplexer #(.width(32), .disabled(0), .enable("false")) multiplexer_1 (
    .in0(C_q), .in1(bit_extender_1_out), .out(busW), .sel(mux_c));

  // Notes on the sheet:
  //   Ruta de datos
  //   contents of rom_1 (hex, n*v repeats v):
  //   93880001 93880002 93880003 91940004 81900005 80140006 80008007 440 60 80 a0 c0 e0
  //   contents of rom_2 (hex, n*v repeats v):
  //   1 1 2 4 3 3
  //   Unidad de Control
  //   contents of rom_3 (hex, n*v repeats v):
  //   18 18 4 0 0 0 4*3
endmodule
