// Logisim project 839841-multi2.circ as structural Verilog: 3 circuits, main circuit main
module BR4 (
  input  regWr,
  input  clk,
  input  reset,
  input  [31:0] busW,
  input  [1:0] RA,
  input  [1:0] RW,
  input  [1:0] RB,
  output [31:0] busA,
  output [31:0] busB
);

  wire decoder_1_out0, decoder_1_out1, decoder_1_out2, decoder_1_out3;
  wire [31:0] register_1_q, register_2_q, register_3_q, register_4_q;

  Decoder #(.select(2), .disabled(0)) decoder_1 (
    .out0(decoder_1_out0), .out1(decoder_1_out1), .out2(decoder_1_out2), .out3(decoder_1_out3), .sel(RW),
    .en(regWr));
  Register #(.width(32)) register_1 (.D(busW), .en(decoder_1_out0), .Q(register_1_q), .clk(clk), .clr(reset));
  Register #(.width(32)) register_2 (.D(busW), .en(decoder_1_out1), .Q(register_2_q), .clk(clk), .clr(reset));
  Register #(.width(32)) register_3 (.D(busW), .en(decoder_1_out2), .Q(register_3_q), .clk(clk), .clr(reset));
  Register #(.width(32)) register_4 (.D(busW), .en(decoder_1_out3), .Q(register_4_q), .clk(clk), .clr(reset));
  Multiplexer #(.select(2), .width(32), .enable("false")) multiplexer_1 (
    .in0(register_1_q), .in1(register_2_q), .in2(register_3_q), .in3(register_4_q), .out(busB), .sel(RB));
  Multiplexer #(.select(2), .width(32), .enable("false")) multiplexer_2 (
    .in0(register_1_q), .in1(register_2_q), .in2(register_3_q), .in3(register_4_q), .out(busA), .sel(RA));
endmodule

module BR32 (
  input  reset,
  input  clk,
  input  [31:0] busW,
  input  regWr,
  input  [4:0] RW,
  input  [4:0] RA,
  input  [4:0] RB,
  output [31:0] busA,
  output [31:0] busB
);

  wire decoder_1_out0, decoder_1_out1, decoder_1_out2, decoder_1_out3, decoder_1_out4, decoder_1_out5,
       decoder_1_out6, decoder_1_out7;
  wire [31:0] br4_1_busa, br4_1_busb, br4_2_busa, br4_2_busb, br4_3_busa, br4_3_busb, br4_4_busa, br4_4_busb,
       br4_5_busa, br4_5_busb, br4_6_busa, br4_6_busb, br4_7_busa, br4_7_busb, br4_8_busa, br4_8_busb;

  Decoder #(.select(3), .disabled(0)) decoder_1 (
    .out0(decoder_1_out0), .out1(decoder_1_out1), .out2(decoder_1_out2), .out3(decoder_1_out3),
    .out4(decoder_1_out4), .out5(decoder_1_out5), .out6(decoder_1_out6), .out7(decoder_1_out7),
    .sel(RW[2:0]), .en(regWr));
  BR4 br4_1 (
    .regWr(decoder_1_out0), .clk(clk), .reset(reset), .busW(busW), .RW(RW[4:3]), .RB(RB[4:3]), .RA(RA[4:3]),
    .busA(br4_1_busa), .busB(br4_1_busb));
  BR4 br4_2 (
    .regWr(decoder_1_out1), .clk(clk), .reset(reset), .busW(busW), .RW(RW[4:3]), .RB(RB[4:3]), .RA(RA[4:3]),
    .busA(br4_2_busa), .busB(br4_2_busb));
  BR4 br4_3 (
    .regWr(decoder_1_out2), .clk(clk), .reset(reset), .busW(busW), .RW(RW[4:3]), .RB(RB[4:3]), .RA(RA[4:3]),
    .busA(br4_3_busa), .busB(br4_3_busb));
  BR4 br4_4 (
    .regWr(decoder_1_out3), .clk(clk), .reset(reset), .busW(busW), .RW(RW[4:3]), .RB(RB[4:3]), .RA(RA[4:3]),
    .busA(br4_4_busa), .busB(br4_4_busb));
  BR4 br4_5 (
    .regWr(decoder_1_out4), .clk(clk), .reset(reset), .busW(busW), .RW(RW[4:3]), .RB(RB[4:3]), .RA(RA[4:3]),
    .busA(br4_5_busa), .busB(br4_5_busb));
  BR4 br4_6 (
    .regWr(decoder_1_out5), .clk(clk), .reset(reset), .busW(busW), .RW(RW[4:3]), .RB(RB[4:3]), .RA(RA[4:3]),
    .busA(br4_6_busa), .busB(br4_6_busb));
  BR4 br4_7 (
    .regWr(decoder_1_out6), .clk(clk), .reset(reset), .busW(busW), .RW(RW[4:3]), .RB(RB[4:3]), .RA(RA[4:3]),
    .busA(br4_7_busa), .busB(br4_7_busb));
  BR4 br4_8 (
    .regWr(decoder_1_out7), .clk(clk), .reset(reset), .busW(busW), .RW(RW[4:3]), .RB(RB[4:3]), .RA(RA[4:3]),
    .busA(br4_8_busa), .busB(br4_8_busb));
  Multiplexer #(.select(3), .width(32), .enable("false")) multiplexer_1 (
    .in0(br4_1_busa), .in1(br4_2_busa), .in2(br4_3_busa), .in3(br4_4_busa), .in4(br4_5_busa),
    .in5(br4_6_busa), .in6(br4_7_busa), .in7(br4_8_busa), .out(busA), .sel(RA[2:0]));
  Multiplexer #(.select(3), .width(32), .enable("false")) multiplexer_2 (
    .in0(br4_1_busb), .in1(br4_2_busb), .in2(br4_3_busb), .in3(br4_4_busb), .in4(br4_5_busb),
    .in5(br4_6_busb), .in6(br4_7_busb), .in7(br4_8_busb), .out(busB), .sel(RB[2:0]));

  // Other names for the same wires on the sheet: RA_prime[2:0] = RA[2:0]; RA_t[1:0] = RA[4:3];
  //   RB_prime[2:0] = RB[2:0]; RB_t[1:0] = RB[4:3]; RW_prime[2:0] = RW[2:0]; RW_t[1:0] = RW[4:3]
endmodule

module main (
  output FZ
);

  wire and_1_out, BEQ, IR, MDR, MemWr, mux_ir, mux_RW, not_1_out, PC, RA, RB, RC, regWr, reloj, reset;
  wire [1:0] mux_busW;
  wire [2:0] CO, rom_2_data;
  wire [4:0] RW;
  wire [5:3] A_q;
  wire [15:0] A15_0, counter_1_q, multiplexer_1_out;
  wire [25:0] register_1_q;
  wire [28:0] rom_1_data;
  wire [31:0] adder_1_out, bit_extender_1_out, br32_1_busa, br32_1_busb, busW, C_q, Din, MDR_q, ram_1_data;
  wire [31:16] A_2_q;

  Button button_1 (.out(reset));
  Clock clock_1 (.out(reloj));
  Counter #(.width(16), .max('hffff)) counter_1 (
    .load(and_1_out), .D(register_1_q[15:0]), .count(PC), .Q(counter_1_q), .clk(reloj), .clr(reset));  // open: carry
  // tty_ctrl tty_ctrl_1: pin names not known
  // TTY tty_1: pin names not known; wires that end beside it: A15_0, MemWr, Din[6:0], reloj
  Multiplexer #(.width(16), .disabled(0), .enable("false")) multiplexer_1 (
    .in0(counter_1_q), .in1(register_1_q[15:0]), .out(multiplexer_1_out), .sel(mux_ir));
  // Probe on CO
  ROM #(.addrWidth(16), .dataWidth(29)) rom_1 (.addr(multiplexer_1_out), .data(rom_1_data));  // open: sel
  and and_1 (and_1_out, BEQ, FZ);
  // RTL2_Viewer rtl2_viewer_1: pin names not known; wires that end beside it: MDR, A15_0, MemWr, Din, CO, register_1_q[25:21], register_1_q[20:16]
  ROM #(.addrWidth(6), .dataWidth(3)) rom_2 (.addr({A_q, CO}), .data(rom_2_data));  // open: sel
  // Probe on CO
  Register #(.width(29)) register_1 (.D(rom_1_data), .en(IR), .Q({CO, register_1_q}), .clk(reloj), .clr(reset));
  // Probe on register_1_q[25:21]
  // Probe on register_1_q[20:16]
  Multiplexer #(.width(5), .disabled(0), .enable("false")) multiplexer_2 (
    .in0(register_1_q[20:16]), .in1(register_1_q[15:11]), .out(RW), .sel(mux_RW));
  Register #(.width(3)) A (.D(rom_2_data), .Q(A_q), .clk(reloj), .clr(reset));  // open: en
  // RTL1_Viewer rtl1_viewer_1: pin names not known; wires that end beside it: busW, RW, regWr
  // Probe on {A_2_q, A15_0}
  BR32 br32_1 (
    .regWr(regWr), .reset(reset), .clk(reloj), .busW(busW), .busA(br32_1_busa), .busB(br32_1_busb), .RW(RW),
    .RA(register_1_q[25:21]), .RB(register_1_q[20:16]));
  Register #(.width(32)) A_2 (.D(br32_1_busa), .en(RA), .Q({A_2_q, A15_0}), .clk(reloj), .clr(reset));
  // Probe on Din
  Register #(.width(32)) B (.D(br32_1_busb), .en(RB), .Q(Din), .clk(reloj), .clr(reset));
  ROM #(.addrWidth(3), .dataWidth(13)) rom_3 (
    .addr(A_q), .data({IR, PC, RA, RB, RC, regWr, mux_busW, MemWr, MDR, mux_ir, mux_RW, BEQ}));  // open: sel
  Adder #(.width(32)) adder_1 (.a({A_2_q, A15_0}), .b(Din), .out(adder_1_out));  // open: cin, cout
  Comparator #(.width(32)) comparator_1 (.a({A_2_q, A15_0}), .b(Din), .eq(FZ));  // open: gt, lt
  not not_1 (not_1_out, MemWr);
  Register #(.width(32)) C (.D(adder_1_out), .en(RC), .Q(C_q), .clk(reloj), .clr(reset));
  assign bit_extender_1_out = {{16{1'b0}}, register_1_q[15:0]};  // Bit_Extender bit_extender_1
  RAM #(.addrWidth(24), .dataWidth(32), .bus("separate")) ram_1 (
    .addr({A_2_q[23:16], A15_0}), .din(Din), .data(ram_1_data), .str(MemWr), .clk(reloj), .ld(not_1_out),
    .clr(reset));  // open: sel
  Register #(.width(32)) u_MDR (.D(ram_1_data), .en(MDR), .Q(MDR_q), .clk(reloj), .clr(reset));
  Multiplexer #(.select(2), .width(32), .disabled(0), .enable("false")) multiplexer_3 (
    .in0(C_q), .in1(bit_extender_1_out), .in2(MDR_q), .out(busW), .sel(mux_busW));  // open: in3
  Counter #(.width(16), .max('hffff)) counter_2 (.count(1'b1), .clk(reloj), .clr(reset));  // open: load, D, Q, carry

  // Other names for the same wires on the sheet: Din6_0[6:0] = Din[6:0]

  // Notes on the sheet:
  //   Ruta de datos
  //   contents of rom_1 (hex, n*v repeats v):
  //   2a 10000 20030 10020009 8030000 4610800 30001 4030000 10000003 8430000 20000 c410000 ffff 2004e
  //   4004f 50020 6004b 10230017 c020000 c040000 c050000 c040000 c060000 c040000 c060000
  //   contents of rom_2 (hex, n*v repeats v):
  //   8*1 5 2 2 6 7 4*0 3 4
  //   Unidad de Control
  //   contents of rom_3 (hex, n*v repeats v):
  //   1800 600 108 82 c0 a0 10 1005
endmodule
