// Logisim project 839841-seg.circ as structural Verilog: 3 circuits, main circuit main
module BR4 (
  input  regWr,
  input  clk,
  input  reset,
  input  [31:0] busW,
  input  [1:0] RA,
  input  [1:0] RW,
  input  [1:0] RB,
  output [31:0] busA,
  output [31:0] busB
);

  wire decoder_1_out0, decoder_1_out1, decoder_1_out2, decoder_1_out3;
  wire [31:0] register_1_q, register_2_q, register_3_q, register_4_q;

  Decoder #(.select(2), .disabled(0)) decoder_1 (
    .out0(decoder_1_out0), .out1(decoder_1_out1), .out2(decoder_1_out2), .out3(decoder_1_out3), .sel(RW),
    .en(regWr));
  Register #(.width(32)) register_1 (.D(busW), .en(decoder_1_out0), .Q(register_1_q), .clk(clk), .clr(reset));
  Register #(.width(32)) register_2 (.D(busW), .en(decoder_1_out1), .Q(register_2_q), .clk(clk), .clr(reset));
  Register #(.width(32)) register_3 (.D(busW), .en(decoder_1_out2), .Q(register_3_q), .clk(clk), .clr(reset));
  Register #(.width(32)) register_4 (.D(busW), .en(decoder_1_out3), .Q(register_4_q), .clk(clk), .clr(reset));
  Multiplexer #(.select(2), .width(32), .enable("false")) multiplexer_1 (
    .in0(register_1_q), .in1(register_2_q), .in2(register_3_q), .in3(register_4_q), .out(busB), .sel(RB));
  Multiplexer #(.select(2), .width(32), .enable("false")) multiplexer_2 (
    .in0(register_1_q), .in1(register_2_q), .in2(register_3_q), .in3(register_4_q), .out(busA), .sel(RA));
endmodule

module BR32 (
  input  reset,
  input  clk,
  input  [31:0] busW,
  input  regWr,
  input  [4:0] RW,
  input  [4:0] RA,
  input  [4:0] RB,
  output [31:0] busA,
  output [31:0] busB
);

  wire decoder_1_out0, decoder_1_out1, decoder_1_out2, decoder_1_out3, decoder_1_out4, decoder_1_out5,
       decoder_1_out6, decoder_1_out7;
  wire [31:0] br4_1_busa, br4_1_busb, br4_2_busa, br4_2_busb, br4_3_busa, br4_3_busb, br4_4_busa, br4_4_busb,
       br4_5_busa, br4_5_busb, br4_6_busa, br4_6_busb, br4_7_busa, br4_7_busb, br4_8_busa, br4_8_busb;

  Decoder #(.select(3), .disabled(0)) decoder_1 (
    .out0(decoder_1_out0), .out1(decoder_1_out1), .out2(decoder_1_out2), .out3(decoder_1_out3),
    .out4(decoder_1_out4), .out5(decoder_1_out5), .out6(decoder_1_out6), .out7(decoder_1_out7),
    .sel(RW[2:0]), .en(regWr));
  BR4 br4_1 (
    .regWr(decoder_1_out0), .clk(clk), .reset(reset), .busW(busW), .RW(RW[4:3]), .RB(RB[4:3]), .RA(RA[4:3]),
    .busA(br4_1_busa), .busB(br4_1_busb));
  BR4 br4_2 (
    .regWr(decoder_1_out1), .clk(clk), .reset(reset), .busW(busW), .RW(RW[4:3]), .RB(RB[4:3]), .RA(RA[4:3]),
    .busA(br4_2_busa), .busB(br4_2_busb));
  BR4 br4_3 (
    .regWr(decoder_1_out2), .clk(clk), .reset(reset), .busW(busW), .RW(RW[4:3]), .RB(RB[4:3]), .RA(RA[4:3]),
    .busA(br4_3_busa), .busB(br4_3_busb));
  BR4 br4_4 (
    .regWr(decoder_1_out3), .clk(clk), .reset(reset), .busW(busW), .RW(RW[4:3]), .RB(RB[4:3]), .RA(RA[4:3]),
    .busA(br4_4_busa), .busB(br4_4_busb));
  BR4 br4_5 (
    .regWr(decoder_1_out4), .clk(clk), .reset(reset), .busW(busW), .RW(RW[4:3]), .RB(RB[4:3]), .RA(RA[4:3]),
    .busA(br4_5_busa), .busB(br4_5_busb));
  BR4 br4_6 (
    .regWr(decoder_1_out5), .clk(clk), .reset(reset), .busW(busW), .RW(RW[4:3]), .RB(RB[4:3]), .RA(RA[4:3]),
    .busA(br4_6_busa), .busB(br4_6_busb));
  BR4 br4_7 (
    .regWr(decoder_1_out6), .clk(clk), .reset(reset), .busW(busW), .RW(RW[4:3]), .RB(RB[4:3]), .RA(RA[4:3]),
    .busA(br4_7_busa), .busB(br4_7_busb));
  BR4 br4_8 (
    .regWr(decoder_1_out7), .clk(clk), .reset(reset), .busW(busW), .RW(RW[4:3]), .RB(RB[4:3]), .RA(RA[4:3]),
    .busA(br4_8_busa), .busB(br4_8_busb));
  Multiplexer #(.select(3), .width(32), .enable("false")) multiplexer_1 (
    .in0(br4_1_busa), .in1(br4_2_busa), .in2(br4_3_busa), .in3(br4_4_busa), .in4(br4_5_busa),
    .in5(br4_6_busa), .in6(br4_7_busa), .in7(br4_8_busa), .out(busA), .sel(RA[2:0]));
  Multiplexer #(.select(3), .width(32), .enable("false")) multiplexer_2 (
    .in0(br4_1_busb), .in1(br4_2_busb), .in2(br4_3_busb), .in3(br4_4_busb), .in4(br4_5_busb),
    .in5(br4_6_busb), .in6(br4_7_busb), .in7(br4_8_busb), .out(busB), .sel(RB[2:0]));

  // Other names for the same wires on the sheet: RA_prime[2:0] = RA[2:0]; RA_t[1:0] = RA[4:3];
  //   RB_prime[2:0] = RB[2:0]; RB_t[1:0] = RB[4:3]; RW_prime[2:0] = RW[2:0]; RW_t[1:0] = RW[4:3]
endmodule

module main (
);

  wire and_1_out, B_EX, B_MEM, BEQ, FZ, IR, K_EX, K_MEM, K_WB, MDR, MemWr, mux_RW, not_1_out, not_2_out, PC,
       RA_EX, RA_MEM, RB, RC_MEM, RC_WB, RD, regWr, reloj, reset, W_MEM, W_WB;
  wire [1:0] mux_busW;
  wire [2:0] CO;
  wire [4:0] multiplexer_1_out, RB_q, RD_q, RW, RW_q;
  wire [15:0] A15_0, counter_2_q;
  wire [22:0] EX_q, rom_1_data, WB_q;
  wire [22:2] MEM_q;
  wire [25:0] IR_q;
  wire [28:0] rom_2_data;
  wire [31:0] A_q, adder_1_out, B_q, bit_extender_1_out, br32_1_busa, br32_1_busb, busW, C_2_q, C_q, Din,
       K_2_q, K_3_q, K_q, MDR_q, ram_1_data;
  wire [31:16] A_2_q;

  not not_1 (not_1_out, and_1_out);
  Counter counter_1 (.count(1'b1), .clk(reloj), .clr(reset));  // open: load, D, Q, carry
  // Probe on CO
  Counter #(.width(16), .max('hffff)) counter_2 (
    .load(and_1_out), .D(IR_q[15:0]), .count(not_1_out), .Q(counter_2_q), .clk(reloj), .clr(reset));  // open: carry
  and and_1 (and_1_out, BEQ, FZ);
  Button button_1 (.out(reset));
  Clock clock_1 (.out(reloj));
  ROM #(.addrWidth(3), .dataWidth(23)) rom_1 (
    .addr(CO), .data({rom_1_data[22], BEQ, IR, PC, B_EX, RA_EX, K_EX, RB, RD, rom_1_data[13:0]}));  // open: sel
  ROM #(.addrWidth(16), .dataWidth(29)) rom_2 (.addr(counter_2_q), .data(rom_2_data));  // open: sel
  Register #(.width(29)) u_IR (.D(rom_2_data), .en(IR), .Q({CO, IR_q}), .clk(reloj), .clr(reset));
  Register #(.width(23)) EX (
    .D({rom_1_data[22], BEQ, IR, PC, B_EX, RA_EX, K_EX, RB, RD, rom_1_data[13:0]}), .en(1'b1),
    .Q({EX_q[22:14], W_MEM, B_MEM, RA_MEM, K_MEM, mux_RW, RC_MEM, EX_q[7:0]}), .clk(reloj), .clr(reset));
  // Probe on IR_q[25:21]
  // Probe on CO
  // Probe on IR_q[20:16]
  assign bit_extender_1_out = {{16{1'b0}}, IR_q[15:0]};  // Bit_Extender bit_extender_1
  Register #(.width(23)) MEM (
    .D({EX_q[22:14], W_MEM, B_MEM, RA_MEM, K_MEM, mux_RW, RC_MEM, EX_q[7:0]}), .en(1'b1),
    .Q({MEM_q[22:8], MemWr, MEM_q[6:5], K_WB, RC_WB, MEM_q[2], W_WB, MDR}), .clk(reloj), .clr(reset));
  Register #(.width(32)) A (.D(br32_1_busa), .en(RA_EX), .Q(A_q), .clk(reloj), .clr(reset));
  BR32 br32_1 (
    .regWr(regWr), .reset(reset), .clk(reloj), .busW(busW), .busA(br32_1_busa), .busB(br32_1_busb), .RW(RW),
    .RA(IR_q[25:21]), .RB(IR_q[20:16]));
  Register #(.width(32)) B (.D(br32_1_busb), .en(B_EX), .Q(B_q), .clk(reloj), .clr(reset));
  Register #(.width(32)) K (.D(bit_extender_1_out), .en(K_EX), .Q(K_q), .clk(reloj), .clr(reset));
  Register #(.width(5)) u_RB (.D(IR_q[20:16]), .en(RB), .Q(RB_q), .clk(reloj), .clr(reset));
  Register #(.width(5)) u_RD (.D(IR_q[15:11]), .Q(RD_q), .clk(reloj), .clr(reset));  // open: en
  Register #(.width(23)) WB (
    .D({MEM_q[22:8], MemWr, MEM_q[6:5], K_WB, RC_WB, MEM_q[2], W_WB, MDR}), .en(1'b1),
    .Q({WB_q[22:7], mux_busW, WB_q[4:3], regWr, WB_q[1:0]}), .clk(reloj), .clr(reset));
  Adder #(.width(32)) adder_1 (.a(A_q), .b(B_q), .out(adder_1_out));  // open: cin, cout
  Comparator #(.width(32)) comparator_1 (.a(br32_1_busa), .b(br32_1_busb), .eq(FZ));  // open: gt, lt
  Multiplexer #(.width(5), .disabled(0), .enable("false")) multiplexer_1 (
    .in0(RB_q), .in1(RD_q), .out(multiplexer_1_out), .sel(mux_RW));
  Register #(.width(32)) A_2 (.D(A_q), .en(RA_MEM), .Q({A_2_q, A15_0}), .clk(reloj), .clr(reset));
  Register #(.width(32)) C (.D(adder_1_out), .en(RC_MEM), .Q(C_q), .clk(reloj), .clr(reset));
  Register #(.width(32)) B_2 (.D(B_q), .en(B_MEM), .Q(Din), .clk(reloj), .clr(reset));
  Register #(.width(32)) K_2 (.D(K_q), .en(K_MEM), .Q(K_2_q), .clk(reloj), .clr(reset));
  Register #(.width(5)) u_RW (.D(multiplexer_1_out), .en(W_MEM), .Q(RW_q), .clk(reloj), .clr(reset));
  // tty_ctrl tty_ctrl_1: pin names not known
  // TTY #(.rows(4), .cols(8)) tty_1: pin names not known; wires that end beside it: A15_0, MemWr, Din[6:0], reloj
  RAM #(.addrWidth(24), .dataWidth(32), .bus("separate")) ram_1 (
    .addr({A_2_q[23:16], A15_0}), .din(Din), .data(ram_1_data), .str(MemWr), .clk(reloj), .ld(not_2_out));  // open: sel, clr
  not not_2 (not_2_out, MemWr);
  Register #(.width(32)) u_MDR (.D(ram_1_data), .en(MDR), .Q(MDR_q), .clk(reloj), .clr(reset));
  Register #(.width(32)) C_2 (.D(C_q), .en(RC_WB), .Q(C_2_q), .clk(reloj), .clr(reset));
  Register #(.width(32)) K_3 (.D(K_2_q), .en(K_WB), .Q(K_3_q), .clk(reloj), .clr(reset));
  Register #(.width(5)) RW_2 (.D(RW_q), .en(W_WB), .Q(RW), .clk(reloj), .clr(reset));
  // RTL1_Viewer rtl1_viewer_1: pin names not known; wires that end beside it: busW, RW, regWr
  // RTL2_Viewer rtl2_viewer_1: pin names not known; wires that end beside it: MDR, A15_0, MemWr, Din
  Multiplexer #(.select(2), .width(32), .disabled(0), .enable("false")) multiplexer_2 (
    .in0(C_2_q), .in1(K_3_q), .in2(MDR_q), .out(busW), .sel(mux_busW));  // open: in3

  // Other names for the same wires on the sheet: Din6_0[6:0] = Din[6:0]

  // Notes on the sheet:
  //   Ruta de datos
  //   Unidad de Control
  //   contents of rom_1 (hex, n*v repeats v):
  //   19a436 1e730e 1aa847 1e1880 7e0000 3e0000 180000
  //   contents of rom_2 (hex, n*v repeats v):
  //   2a 10000 20030 18000000 18000000 18000000 10020015 18000000 8030000 18000000 18000000 18000000
  //   4610800 30001 18000000 18000000 18000000 4030000 18000000 10210006 18000000 8430000 20000 18000000
  //   18000000 18000000 c410000 ffff 2004e 4004f 50020 c020000 6004b 10230026 18000000 c020000 c040000
  //   c050000 c040000 c060000
  //   IF/ID
  //   ID/EX
  //   EX/MEM
  //   MEM/WB
endmodule
