// Logisim project 839841-cache.circ as structural Verilog: 1 circuit, main circuit main
module main (
  input  in_1
);

  wire cache_test4_1_ok, clk, comparator_2_eq, hit, mem_en, MemWr, not_1_out, or_1_out, reg0, reg1, reg2,
       reg3, w0, w1, way, way_0, way_1, way_choose;
  wire [2:0] cache_test4_1_err;
  wire [3:0] counter_1_q;
  wire [6:0] cache_test4_1_ciclo;
  wire [7:0] counter_2_q, ram_1_data, ram_3_data;
  wire [15:0] dir;
  wire [31:0] inst, main_1_p5, multiplexer_1_out, multiplexer_2_out, ram_4_data, ram_5_data, ram_6_data,
       ram_7_data, ram_8_data, ram_9_data, ram_10_data, ram_11_data, register_1_q, register_2_q,
       register_3_q, register_4_q;

  not not_1 (not_1_out, way);
  not not_2 (mem_en, hit);
  Counter #(.width(4), .max('hf)) counter_1 (
    .count(1'b1), .Q(counter_1_q), .clk(clk), .clr(or_1_out));  // open: load, D, carry
  or or_1 (or_1_out, hit, in_1);
  RAM #(.addrWidth(5), .bus("separate")) ram_1 (
    .addr(dir[8:4]), .din({dir[15:9], 1'b1}), .data(ram_1_data), .str(w1), .clk(clk), .clr(in_1));  // open: sel, ld
  Decoder #(.select(4), .enable("false")) decoder_1 (
    .out4(reg0), .out6(reg1), .out8(reg2), .out10(reg3), .out11(MemWr), .sel(counter_1_q));  // open: out0, out1, out2, out3, out5, out7, out9, out12, out13, out14, out15
  RAM #(.addrWidth(5), .dataWidth(1), .bus("separate")) ram_2 (
    .addr(dir[8:4]), .din(not_1_out), .data(way), .str(MemWr), .clk(clk), .clr(in_1));  // open: sel, ld
  Comparator comparator_1 (.a(ram_1_data), .b({dir[15:9], 1'b1}), .eq(way_choose));  // open: gt, lt
  // Probe on cache_test4_1_ok
  Decoder #(.enable("false")) decoder_2 (.out0(way_0), .out1(way_1), .sel(way));
  // Probe on cache_test4_1_err
  // Probe on cache_test4_1_ciclo
  cache_test4 cache_test4_1 (
    .clk(clk), .reset(in_1), .inst(inst), .OK(cache_test4_1_ok), .in_3(dir), .ERR(cache_test4_1_err),
    .ciclo(cache_test4_1_ciclo), .hit(hit), .way(way_choose), .set(dir[8:4]), .nia(20'hcd0a1));
  // Probe on 20'hcd0a1
  Comparator comparator_2 (.a(ram_3_data), .b({dir[15:9], 1'b1}), .eq(comparator_2_eq));  // open: gt, lt
  or or_2 (hit, way_choose, comparator_2_eq);
  Counter counter_2 (.count(hit), .Q(counter_2_q), .clk(clk), .clr(in_1));  // open: load, D, carry
  RAM #(.addrWidth(5), .bus("separate")) ram_3 (
    .addr(dir[8:4]), .din({dir[15:9], 1'b1}), .data(ram_3_data), .str(w0), .clk(clk), .clr(in_1));  // open: sel, ld
  ROM #(.dataWidth(16)) rom_1 (.addr(counter_2_q), .data(dir));  // open: sel
  and and_1 (w0, MemWr, way_0);
  and and_2 (w1, MemWr, way_1);
  // Probe on main_1_p5
  // MP_main main_1: pin names not known; wires that end beside it: dir, mem_en, clk, in_1, main_1_p5
  Register #(.width(32)) register_1 (.D(main_1_p5), .en(reg0), .Q(register_1_q), .clk(clk), .clr(in_1));
  Register #(.width(32)) register_2 (.D(main_1_p5), .en(reg1), .Q(register_2_q), .clk(clk), .clr(in_1));
  Register #(.width(32)) register_3 (.D(main_1_p5), .en(reg2), .Q(register_3_q), .clk(clk), .clr(in_1));
  Register #(.width(32)) register_4 (.D(main_1_p5), .en(reg3), .Q(register_4_q), .clk(clk), .clr(in_1));
  RAM #(.addrWidth(5), .dataWidth(32), .bus("separate")) ram_4 (
    .addr(dir[8:4]), .din(register_1_q), .data(ram_4_data), .str(w0), .clk(clk), .clr(in_1));  // open: sel, ld
  RAM #(.addrWidth(5), .dataWidth(32), .bus("separate")) ram_5 (
    .addr(dir[8:4]), .din(register_1_q), .data(ram_5_data), .str(w1), .clk(clk), .clr(in_1));  // open: sel, ld
  RAM #(.addrWidth(5), .dataWidth(32), .bus("separate")) ram_6 (
    .addr(dir[8:4]), .din(register_2_q), .data(ram_6_data), .str(w0), .clk(clk), .clr(in_1));  // open: sel, ld
  RAM #(.addrWidth(5), .dataWidth(32), .bus("separate")) ram_7 (
    .addr(dir[8:4]), .din(register_2_q), .data(ram_7_data), .str(w1), .clk(clk), .clr(in_1));  // open: sel, ld
  RAM #(.addrWidth(5), .dataWidth(32), .bus("separate")) ram_8 (
    .addr(dir[8:4]), .din(register_3_q), .data(ram_8_data), .str(w0), .clk(clk), .clr(in_1));  // open: sel, ld
  RAM #(.addrWidth(5), .dataWidth(32), .bus("separate")) ram_9 (
    .addr(dir[8:4]), .din(register_3_q), .data(ram_9_data), .str(w1), .clk(clk), .clr(in_1));  // open: sel, ld
  RAM #(.addrWidth(5), .dataWidth(32), .bus("separate")) ram_10 (
    .addr(dir[8:4]), .din(register_4_q), .data(ram_10_data), .str(w0), .clk(clk), .clr(in_1));  // open: sel, ld
  RAM #(.addrWidth(5), .dataWidth(32), .bus("separate")) ram_11 (
    .addr(dir[8:4]), .din(register_4_q), .data(ram_11_data), .str(w1), .clk(clk), .clr(in_1));  // open: sel, ld
  Multiplexer #(.select(2), .width(32), .enable("false")) multiplexer_1 (
    .in0(ram_4_data), .in1(ram_6_data), .in2(ram_8_data), .in3(ram_10_data), .out(multiplexer_1_out),
    .sel(dir[3:2]));
  Multiplexer #(.select(2), .width(32), .enable("false")) multiplexer_2 (
    .in0(ram_5_data), .in1(ram_7_data), .in2(ram_9_data), .in3(ram_11_data), .out(multiplexer_2_out),
    .sel(dir[3:2]));
  Clock clock_1 (.out(clk));
  Multiplexer #(.width(32), .enable("false")) multiplexer_3 (
    .in0(multiplexer_1_out), .in1(multiplexer_2_out), .out(inst), .sel(way_choose));

  // Other names for the same wires on the sheet: mux[1:0] = dir[3:2]; set[4:0] = dir[8:4]; reset = in_1;
  //   tag[6:0] = dir[15:9]; tag_v[7:1] = dir[15:9]

  // Notes on the sheet:
  //   Unidad de Control
  //   contents of rom_1 (hex, n*v repeats v):
  //   200 400 600 404 b40 f40 1340 1344 2000 3000 4000 3004
endmodule
