// Logisim project wuolah-free-p3.circ as structural Verilog: 4 circuits, main circuit main
module BR4 (
  input  clk,
  input  [31:0] BusW,
  input  [1:0] RA,
  input  RegW,
  input  [1:0] RW,
  input  [1:0] RB,
  input  reset,
  output [31:0] busA,
  output [31:0] busB
);

  wire decoder_1_out0, decoder_1_out1, decoder_1_out2, decoder_1_out3;
  wire [31:0] register_1_q, register_2_q, register_3_q, register_4_q;

  Decoder #(.select(2), .disabled(0)) decoder_1 (
    .out0(decoder_1_out0), .out1(decoder_1_out1), .out2(decoder_1_out2), .out3(decoder_1_out3), .sel(RW),
    .en(RegW));
  Register #(.width(32)) register_1 (.D(BusW), .en(decoder_1_out0), .Q(register_1_q), .clk(clk), .clr(reset));
  Register #(.width(32)) register_2 (.D(BusW), .en(decoder_1_out1), .Q(register_2_q), .clk(clk), .clr(reset));
  Register #(.width(32)) register_3 (.D(BusW), .en(decoder_1_out2), .Q(register_3_q), .clk(clk), .clr(reset));
  Register #(.width(32)) register_4 (.D(BusW), .en(decoder_1_out3), .Q(register_4_q), .clk(clk), .clr(reset));
  Multiplexer #(.select(2), .width(32), .enable("false")) multiplexer_1 (
    .in0(register_1_q), .in1(register_2_q), .in2(register_3_q), .in3(register_4_q), .out(busA), .sel(RA));
  Multiplexer #(.select(2), .width(32), .enable("false")) multiplexer_2 (
    .in0(register_1_q), .in1(register_2_q), .in2(register_3_q), .in3(register_4_q), .out(busB), .sel(RB));

  // Other names for the same wires on the sheet: bus[31:0] = BusW
endmodule

module BR32 (
  input  clk,
  input  [31:0] busW,
  input  reset,
  input  regW,
  input  [4:0] RW,
  input  [4:0] RA,
  input  [4:0] RB,
  output [31:0] busA,
  output [31:0] busB
);

  wire decoder_1_out0, decoder_1_out1, decoder_1_out2, decoder_1_out3, decoder_1_out4, decoder_1_out5,
       decoder_1_out6, decoder_1_out7;
  wire [31:0] br4_1_busa, br4_1_busb, br4_2_busa, br4_2_busb, br4_3_busa, br4_3_busb, br4_4_busa, br4_4_busb,
       br4_5_busa, br4_5_busb, br4_6_busa, br4_6_busb, br4_7_busa, br4_7_busb, br4_8_busa, br4_8_busb;

  Decoder #(.select(3), .disabled(0)) decoder_1 (
    .out0(decoder_1_out0), .out1(decoder_1_out1), .out2(decoder_1_out2), .out3(decoder_1_out3),
    .out4(decoder_1_out4), .out5(decoder_1_out5), .out6(decoder_1_out6), .out7(decoder_1_out7),
    .sel(RW[4:2]), .en(regW));
  BR4 br4_1 (
    .BusW(busW), .RA(RA[1:0]), .RegW(decoder_1_out0), .RW(RW[1:0]), .RB(RB[1:0]), .clk(clk), .reset(reset),
    .busA(br4_1_busa), .busB(br4_1_busb));
  BR4 br4_2 (
    .BusW(busW), .RA(RA[1:0]), .RegW(decoder_1_out1), .RW(RW[1:0]), .RB(RB[1:0]), .clk(clk), .reset(reset),
    .busA(br4_2_busa), .busB(br4_2_busb));
  BR4 br4_3 (
    .BusW(busW), .RA(RA[1:0]), .RegW(decoder_1_out2), .RW(RW[1:0]), .RB(RB[1:0]), .clk(clk), .reset(reset),
    .busA(br4_3_busa), .busB(br4_3_busb));
  BR4 br4_4 (
    .BusW(busW), .RA(RA[1:0]), .RegW(decoder_1_out3), .RW(RW[1:0]), .RB(RB[1:0]), .clk(clk), .reset(reset),
    .busA(br4_4_busa), .busB(br4_4_busb));
  BR4 br4_5 (
    .BusW(busW), .RA(RA[1:0]), .RegW(decoder_1_out4), .RW(RW[1:0]), .RB(RB[1:0]), .clk(clk), .reset(reset),
    .busA(br4_5_busa), .busB(br4_5_busb));
  BR4 br4_6 (
    .BusW(busW), .RA(RA[1:0]), .RegW(decoder_1_out5), .RW(RW[1:0]), .RB(RB[1:0]), .clk(clk), .reset(reset),
    .busA(br4_6_busa), .busB(br4_6_busb));
  BR4 br4_7 (
    .BusW(busW), .RA(RA[1:0]), .RegW(decoder_1_out6), .RW(RW[1:0]), .RB(RB[1:0]), .clk(clk), .reset(reset),
    .busA(br4_7_busa), .busB(br4_7_busb));
  BR4 br4_8 (
    .BusW(busW), .RA(RA[1:0]), .RegW(decoder_1_out7), .RW(RW[1:0]), .RB(RB[1:0]), .clk(clk), .reset(reset),
    .busA(br4_8_busa), .busB(br4_8_busb));
  Multiplexer #(.select(3), .width(32), .disabled(0), .enable("false")) multiplexer_1 (
    .in0(br4_1_busa), .in1(br4_2_busa), .in2(br4_3_busa), .in3(br4_4_busa), .in4(br4_5_busa),
    .in5(br4_6_busa), .in6(br4_7_busa), .in7(br4_8_busa), .out(busA), .sel(RA[4:2]));
  Multiplexer #(.select(3), .width(32), .disabled(0), .enable("false")) multiplexer_2 (
    .in0(br4_1_busb), .in1(br4_2_busb), .in2(br4_3_busb), .in3(br4_4_busb), .in4(br4_5_busb),
    .in5(br4_6_busb), .in6(br4_7_busb), .in7(br4_8_busb), .out(busB), .sel(RB[4:2]));

  // Other names for the same wires on the sheet: RA_t[1:0] = RA[1:0]; RA_MUX[2:0] = RA[4:2]; RB_t[1:0] = RB[1:0];
  //   RB_MUX[2:0] = RB[4:2]; RW_01[1:0] = RW[1:0]
endmodule

module main (
);

  wire clk, comparator_1_eq, IR, L_prime_E, MDR, not_1_out, PC_1, PC_k, RA, RB, RegW, reset, ROM_ctr, RW_ctr,
       S_out;
  wire [1:0] busW_ctr;
  wire [4:0] RW;
  wire [15:0] A15_0, counter_1_q, IR_q_2, multiplexer_1_out;
  wire [31:0] adder_1_out, bit_extender_1_out, br32_1_busa, br32_1_busb, busW, Din, IR_q, Mem, ram_1_data,
       rom_1_data, Suma;
  wire [31:16] RA_q;

  Clock clock (.out(clk));
  Button u_reset (.out(reset));
  // RTL1_Viewer rtl1_viewer_1: pin names not known; wires that end beside it: busW, RW, RegW
  // tty_ctrl tty_ctrl_1: pin names not known
  // TTY tty_1: pin names not known; wires that end beside it: A15_0, L_prime_E, Din[6:0], clk
  // RTL2_Viewer rtl2_viewer_1: pin names not known; wires that end beside it: MDR, A15_0, L_prime_E, Din
  Counter #(.width(16), .max('hffff)) counter_1 (
    .load(PC_k), .D(IR_q_2), .count(PC_1), .Q(counter_1_q), .clk(clk), .clr(reset));  // open: carry
  Multiplexer #(.width(16), .disabled(0), .enable("false")) multiplexer_1 (
    .in0(counter_1_q), .in1(IR_q_2), .out(multiplexer_1_out), .sel(ROM_ctr));
  Register #(.width(32)) u_IR (.D(rom_1_data), .en(IR), .Q({IR_q[31:26], IR_q_2, IR_q[9:0]}), .clk(clk), .clr(reset));
  ROM #(.addrWidth(16), .dataWidth(32)) rom_1 (.addr(multiplexer_1_out), .data(rom_1_data));  // open: sel
  UC uc_1 (
    .CO(IR_q[31:29]), .clk(clk), .busW_ctr(busW_ctr), .RegW(RegW), .S_out(S_out), .RB(RB), .RA(RA),
    .PC_1(PC_1), .reset(reset), .FZ(comparator_1_eq), .PC_K(PC_k), .ROM_ctr(ROM_ctr), .IR(IR), .MDR(MDR),
    .L_prime_E(L_prime_E), .RW_ctr(RW_ctr));
  assign bit_extender_1_out = {{16{IR_q_2[15]}}, IR_q_2};  // Bit_Extender bit_extender_1
  Multiplexer #(.select(2), .width(32), .disabled(0), .enable("false")) multiplexer_2 (
    .in0(bit_extender_1_out), .in1(Suma), .in2(Mem), .out(busW), .sel(busW_ctr));  // open: in3
  Multiplexer #(.width(5), .disabled(0), .enable("false")) multiplexer_3 (
    .in0(IR_q_2[4:0]), .in1(IR_q[4:0]), .out(RW), .sel(RW_ctr));
  BR32 br32_1 (
    .busW(busW), .reset(reset), .regW(RegW), .RW(RW), .RA(IR_q[9:5]), .RB(IR_q[4:0]), .busA(br32_1_busa),
    .busB(br32_1_busb), .clk(clk));
  Comparator #(.width(32)) comparator_1 (.a(br32_1_busa), .b(br32_1_busb), .eq(comparator_1_eq));  // open: gt, lt
  Register #(.width(32)) u_RA (.D(br32_1_busa), .en(RA), .Q({RA_q, A15_0}), .clk(clk), .clr(reset));
  Register #(.width(32)) u_RB (.D(br32_1_busb), .en(RB), .Q(Din), .clk(clk), .clr(reset));
  Register #(.width(32)) register_1 (.D(adder_1_out), .en(S_out), .Q(Suma), .clk(clk), .clr(reset));
  Adder #(.width(32)) adder_1 (.a({RA_q, A15_0}), .b(Din), .out(adder_1_out));  // open: cin, cout
  RAM #(.addrWidth(16), .dataWidth(32), .bus("separate")) ram_1 (
    .addr(A15_0), .din(Din), .data(ram_1_data), .str(L_prime_E), .clk(clk), .ld(not_1_out), .clr(reset));  // open: sel
  not not_1 (not_1_out, L_prime_E);
  Register #(.width(32)) u_MDR (.D(ram_1_data), .en(MDR), .Q(Mem), .clk(clk), .clr(reset));

  // Other names for the same wires on the sheet: Din6_0[6:0] = Din[6:0]

  // Notes on the sheet:
  //   ESTAN MAL LAS LETRAS REEHACEERLAS
  //   MIRAR COMO SE PONEN EN HEXA
  //   contents of rom_1 (hex, n*v repeats v):
  //   20000000 20000001 20001802 20008403 20000404 40000065 80002c22 5000a0 481 c83 80001442 20000001
  //   60000020 40000022 23fffc01 20013c03 20013804 20012c05 20008006 80005c02 60000024 60000023 60000026
  //   60000023 60000025 80006442
endmodule

module UC (
  input  [2:0] CO,
  input  FZ,
  input  clk,
  input  reset,
  output RW_ctr,
  output RegW,
  output MDR,
  output L_prime_E,
  output S_out,
  output RB,
  output RA,
  output [1:0] busW_ctr,
  output IR,
  output ROM_ctr,
  output PC_K,
  output PC_1
);

  wire [2:0] register_1_q, rom_1_data;

  ROM #(.addrWidth(7), .dataWidth(3)) rom_1 (.addr({register_1_q, FZ, CO}), .data(rom_1_data));  // open: sel
  Register #(.width(3)) register_1 (.D(rom_1_data), .en(1'b1), .Q(register_1_q), .clk(clk), .clr(reset));
  ROM #(.addrWidth(3), .dataWidth(13)) rom_2 (
    .addr(register_1_q),
    .data({PC_1, PC_K, ROM_ctr, IR, busW_ctr, RA, RB, S_out, L_prime_E, MDR, RegW, RW_ctr}));  // open: sel

  // Notes on the sheet:
  //   contents of rom_1 (hex, n*v repeats v):
  //   6*1 0 0 6*1 0 0 2 5 2 6 4*0 2 5 2 6 7 0 0 0 3 0 4 5*0 3 0 4 5*0 6*1 0 0 6*1 0 0 6*1 0 0 6*1 0 0 6*1
  //   0 0 6*1 0 0 6*1 0 0 6*1 0 0 6*1 0 0 6*1
  //   contents of rom_2 (hex, n*v repeats v):
  //   200 1060 14 282 303 203 208 e00
endmodule
